# Fritzing sketch Common Cathode RGB LED Usage (saved by Fritzing 0.9.0b)
breadboards: 1

parts:
  Part1 = Arduino Uno (Rev3)
  RGB_LED_(Common_Cathode) = RGB LED - (4 legs) [package="5 mm [THT]"]
  R1 = Resistor [tolerance=±5% resistance=330 package=THT]
  R2 = Resistor [tolerance=±5% resistance=330 package=THT]
  R3 = Resistor [tolerance=±5% resistance=330 package=THT]

nets:
  N1: Part1.D9_PWM, R1.Pin_1
  N2: Part1.D11_PWM/MOSI, R2.Pin_1
  N3: Part1.D6_PWM, R3.Pin_1
  N4: Part1.GND, RGB_LED_(Common_Cathode).common_anode
  N5: RGB_LED_(Common_Cathode).red_cathode, R2.Pin_0
  N6: RGB_LED_(Common_Cathode).green_cathode, R1.Pin_0
  N7: RGB_LED_(Common_Cathode).blue_cathode, R3.Pin_0
